// Logisim project practica3.circ as structural Verilog
module EJERCICIO_2__SI_SOLO_SI (
  input  P,
  input  Q,
  output RESULTADO
);

  wire and_1_out, and_2_out, not_1_out, not_2_out;

  not not_1 (not_1_out, P);
  not not_2 (not_2_out, Q);
  and and_1 (and_1_out, not_1_out, not_2_out);
  and and_2 (and_2_out, P, Q);
  or or_1 (RESULTADO, and_1_out, and_2_out);

  // Notes on the sheet:
  //   SI SOLO SI
endmodule

module EJERCICIO_1_IMPLICACION (
  input  P,
  input  Q,
  output out_3
);

  wire transistor_1_out;

  Transistor transistor_1 (.in(1'b1), .out(transistor_1_out), .gate(P));
  Transistor #(.\type ("n")) transistor_2 (.in(1'b0), .out(transistor_1_out), .gate(P));
  Transistor transistor_3 (.in(Q), .out(out_3), .gate(transistor_1_out));
  Transistor #(.\type ("n")) transistor_4 (.in(1'b1), .out(out_3), .gate(transistor_1_out));

  // Notes on the sheet:
  //   IMPLICACION
endmodule

module EJERCICIO_3_COMPARADOR (
  input  y_0,
  input  y_1,
  input  x_1,
  input  x_0,
  output x____y
);

  wire and_1_out, and_2_out, and_3_out, and_4_out, and_5_out, not_1_out, not_2_out, not_3_out, not_4_out,
       not_5_out;

  not not_1 (not_1_out, y_0);
  not not_2 (not_2_out, y_1);
  not not_3 (not_3_out, y_0);
  not not_4 (not_4_out, y_0);
  not not_5 (not_5_out, y_1);
  and and_1 (and_1_out, not_1_out, not_2_out);
  and and_2 (and_2_out, x_0, not_3_out);
  and and_3 (and_3_out, x_1, not_4_out);
  and and_4 (and_4_out, x_0, x_1);
  and and_5 (and_5_out, x_0, not_5_out);
  or or_1 (x____y, and_1_out, and_2_out, and_3_out, and_4_out, and_5_out);

  // Notes on the sheet:
  //   X
  //   Y
  //   COMPARADOR
endmodule

module EJERCICIO_4_COMPARADOR (
  input  x1,
  input  x0,
  input  y1,
  input  y0,
  output A_MENOR_B,
  output A_IGUAL_B,
  output A_MAYOR_B
);

  wire and_1_out, and_2_out, and_3_out, and_4_out, and_5_out, and_6_out, and_7_out, and_8_out, and_9_out,
       and_10_out, not_1_out, not_2_out, not_3_out, not_4_out, not_5_out, not_6_out, not_7_out, not_8_out,
       not_9_out, not_10_out, not_11_out, not_12_out, not_13_out, not_14_out, not_15_out, not_16_out;

  not not_1 (not_1_out, x1);
  not not_2 (not_2_out, x0);
  not not_3 (not_3_out, x1);
  not not_4 (not_4_out, x0);
  not not_5 (not_5_out, x1);
  not not_6 (not_6_out, x0);
  not not_7 (not_7_out, y1);
  not not_8 (not_8_out, y0);
  not not_9 (not_9_out, x1);
  not not_10 (not_10_out, y1);
  not not_11 (not_11_out, x0);
  not not_12 (not_12_out, y0);
  not not_13 (not_13_out, y1);
  not not_14 (not_14_out, y0);
  not not_15 (not_15_out, y1);
  not not_16 (not_16_out, y0);
  and and_1 (and_1_out, not_1_out, not_2_out, y0);
  and and_2 (and_2_out, not_3_out, y1);
  and and_3 (and_3_out, not_4_out, y1, y0);
  and and_4 (and_4_out, not_5_out, not_6_out, not_7_out, not_8_out);
  and and_5 (and_5_out, not_9_out, x0, not_10_out, y0);
  and and_6 (and_6_out, x1, not_11_out, y1, not_12_out);
  and and_7 (and_7_out, x1, x0, y1, y0);
  and and_8 (and_8_out, x0, not_13_out, not_14_out);
  and and_9 (and_9_out, x1, not_15_out);
  and and_10 (and_10_out, x1, x0, not_16_out);
  or or_1 (A_MENOR_B, and_1_out, and_2_out, and_3_out);
  or or_2 (A_IGUAL_B, and_4_out, and_5_out, and_6_out, and_7_out);
  or or_3 (A_MAYOR_B, and_8_out, and_9_out, and_10_out);

  // Notes on the sheet:
  //   COMPARADOR
endmodule
