// Logisim project practica4.circ as structural Verilog
module EJERCICIO_2 (
  input  A,
  input  Carry_In,
  input  B,
  output Sum,
  output Carry_Out
);

  wire and_1_out, and_2_out, xor_1_out;

  xor xor_1 (xor_1_out, A, B);
  xor xor_2 (Sum, xor_1_out, Carry_In);
  and and_1 (and_1_out, xor_1_out, Carry_In);
  and and_2 (and_2_out, A, B);
  or or_1 (Carry_Out, and_1_out, and_2_out);
endmodule

module EJERCICIO_3 (
  input  [7:0] A,
  input  [7:0] B,
  input  Carry_In,
  output out_4,
  output [7:0] out_5
);

  wire ejercicio_2_1_carry_out, ejercicio_2_2_carry_out, ejercicio_2_3_carry_out, ejercicio_2_4_carry_out,
       ejercicio_2_5_carry_out, ejercicio_2_6_carry_out, ejercicio_2_7_carry_out;

  EJERCICIO_2 ejercicio_2_1 (
    .A(A[0]), .B(B[0]), .Carry_In(Carry_In), .Carry_Out(ejercicio_2_1_carry_out), .Sum(out_5[0]));
  EJERCICIO_2 ejercicio_2_2 (
    .A(A[1]), .B(B[1]), .Carry_In(ejercicio_2_1_carry_out), .Carry_Out(ejercicio_2_2_carry_out),
    .Sum(out_5[1]));
  EJERCICIO_2 ejercicio_2_3 (
    .A(A[2]), .B(B[2]), .Carry_In(ejercicio_2_2_carry_out), .Carry_Out(ejercicio_2_3_carry_out),
    .Sum(out_5[2]));
  EJERCICIO_2 ejercicio_2_4 (
    .A(A[3]), .B(B[3]), .Carry_In(ejercicio_2_3_carry_out), .Carry_Out(ejercicio_2_4_carry_out),
    .Sum(out_5[3]));
  EJERCICIO_2 ejercicio_2_5 (
    .A(A[4]), .B(B[4]), .Carry_In(ejercicio_2_4_carry_out), .Carry_Out(ejercicio_2_5_carry_out),
    .Sum(out_5[4]));
  EJERCICIO_2 ejercicio_2_6 (
    .A(A[5]), .B(B[5]), .Carry_In(ejercicio_2_5_carry_out), .Carry_Out(ejercicio_2_6_carry_out),
    .Sum(out_5[5]));
  EJERCICIO_2 ejercicio_2_7 (
    .A(A[6]), .B(B[6]), .Carry_In(ejercicio_2_6_carry_out), .Carry_Out(ejercicio_2_7_carry_out),
    .Sum(out_5[6]));
  EJERCICIO_2 ejercicio_2_8 (.A(A[7]), .B(B[7]), .Carry_In(ejercicio_2_7_carry_out), .Carry_Out(out_4), .Sum(out_5[7]));

  // Notes on the sheet:
  //   Carry_Out
endmodule

module EJERCICIO_4 (
  input  Carry_In,
  input  [7:0] in_2,
  input  in_3,
  input  [7:0] in_4,
  output [7:0] Result,
  output Carry_Out
);

  wire ejercicio_3_1_out_4, restador_8_bits_1_out_4;
  wire [7:0] ejercicio_3_1_out_5, restador_8_bits_1_out_5;

  Restador_8_bits restador_8_bits_1 (
    .A(in_2), .B(in_4), .out_5(restador_8_bits_1_out_5), .Carry_In(Carry_In), .out_4(restador_8_bits_1_out_4));
  EJERCICIO_3 ejercicio_3_1 (
    .A(in_2), .B(in_4), .out_5(ejercicio_3_1_out_5), .Carry_In(Carry_In), .out_4(ejercicio_3_1_out_4));
  Multiplexer #(.width(8), .enable("false")) multiplexer_1 (
    .in0(ejercicio_3_1_out_5), .in1(restador_8_bits_1_out_5), .out(Result), .sel(in_3));
  Multiplexer multiplexer_2 (
    .in0(ejercicio_3_1_out_4), .in1(restador_8_bits_1_out_4), .out(Carry_Out), .sel(in_3));  // open: en

  // Notes on the sheet:
  //   A
  //   B
endmodule

module Restador_8_bits (
  input  [7:0] A,
  input  [7:0] B,
  input  Carry_In,
  output out_4,
  output [7:0] out_5
);

  wire restador_1_bit_1_carry_out, restador_1_bit_2_carry_out, restador_1_bit_3_carry_out,
       restador_1_bit_4_carry_out, restador_1_bit_5_carry_out, restador_1_bit_6_carry_out,
       restador_1_bit_7_carry_out;

  Restador_1_bit restador_1_bit_1 (
    .Carry_In(Carry_In), .A(A[0]), .B(B[0]), .Substraction(out_5[0]), .Carry_Out(restador_1_bit_1_carry_out));
  Restador_1_bit restador_1_bit_2 (
    .Carry_In(restador_1_bit_1_carry_out), .A(A[1]), .B(B[1]), .Substraction(out_5[1]),
    .Carry_Out(restador_1_bit_2_carry_out));
  Restador_1_bit restador_1_bit_3 (
    .Carry_In(restador_1_bit_2_carry_out), .A(A[2]), .B(B[2]), .Substraction(out_5[2]),
    .Carry_Out(restador_1_bit_3_carry_out));
  Restador_1_bit restador_1_bit_4 (
    .Carry_In(restador_1_bit_3_carry_out), .A(A[3]), .B(B[3]), .Substraction(out_5[3]),
    .Carry_Out(restador_1_bit_4_carry_out));
  Restador_1_bit restador_1_bit_5 (
    .Carry_In(restador_1_bit_4_carry_out), .A(A[4]), .B(B[4]), .Substraction(out_5[4]),
    .Carry_Out(restador_1_bit_5_carry_out));
  Restador_1_bit restador_1_bit_6 (
    .Carry_In(restador_1_bit_5_carry_out), .A(A[5]), .B(B[5]), .Substraction(out_5[5]),
    .Carry_Out(restador_1_bit_6_carry_out));
  Restador_1_bit restador_1_bit_7 (
    .Carry_In(restador_1_bit_6_carry_out), .A(A[6]), .B(B[6]), .Substraction(out_5[6]),
    .Carry_Out(restador_1_bit_7_carry_out));
  Restador_1_bit restador_1_bit_8 (
    .Carry_In(restador_1_bit_7_carry_out), .A(A[7]), .B(B[7]), .Substraction(out_5[7]), .Carry_Out(out_4));

  // Notes on the sheet:
  //   Carry_Out
endmodule

module Restador_1_bit (
  input  Carry_In,
  input  A,
  input  B,
  output Substraction,
  output Carry_Out
);

  wire and_1_out, and_2_out, not_1_out, not_2_out, xor_1_out;

  not not_1 (not_1_out, A);
  xor xor_1 (xor_1_out, A, B);
  and and_1 (and_1_out, not_1_out, B);
  not not_2 (not_2_out, xor_1_out);
  and and_2 (and_2_out, not_2_out, Carry_In);
  xor xor_2 (Substraction, xor_1_out, Carry_In);
  or or_1 (Carry_Out, and_2_out, and_1_out);
endmodule

module EJERCICIO_5 (
  input  in_1,
  input  [7:0] in_2,
  input  [7:0] in_3,
  input  [7:0] in_4,
  input  [7:0] in_5,
  output [7:0] out_6,
  output out_7
);

  wire ejercicio_3_1_out_4, ejercicio_3_2_out_4;
  wire [7:0] ejercicio_3_1_out_5, ejercicio_3_2_out_5;

  EJERCICIO_3 ejercicio_3_1 (
    .A(in_4), .B(in_5), .out_5(ejercicio_3_1_out_5), .Carry_In(ejercicio_3_2_out_4),
    .out_4(ejercicio_3_1_out_4));
  EJERCICIO_3 ejercicio_3_2 (
    .A(in_2), .B(in_3), .out_5(ejercicio_3_2_out_5), .Carry_In(in_1), .out_4(ejercicio_3_2_out_4));
  Restador_8_bits restador_8_bits_1 (
    .A(ejercicio_3_2_out_5), .B(ejercicio_3_1_out_5), .out_5(out_6), .Carry_In(ejercicio_3_1_out_4),
    .out_4(out_7));

  // Notes on the sheet:
  //   A
  //   B
  //   C
  //   D
endmodule
